# Fritzing sketch breadboard_layouts (saved by Fritzing 1.0.1rc)
breadboards: 2

parts:
  LED1 = smd LED [color="Red (633nm)" package="0603 [SMD]"]
  R1 = Resistor [tolerance=±5% resistance=1k package="1206 [SMD]"]
  LED2 = smd LED [color="Red (633nm)" package="0603 [SMD]"]
  R2 = Resistor [tolerance=±5% resistance=1k package="1206 [SMD]"]
  Raspberry_Pi_2 = Raspberry Pi 5
  Mod1 = Raspberry Pi Pico W

nets:
  N1: LED1.anode, R1.Pin_0
  N2: R1.Pin_1, Mod1.pin_26
  N3: LED2.anode, R2.Pin_0
  N4: R2.Pin_1, Raspberry_Pi_2.GPIO21

notes:
  USB

custom parts:
  Raspberry Pi 5: The RPi5, a faster version of the awesome Raspberry Pi4B ARM Board with 40 pin gpio.
  Raspberry Pi Pico W: Raspberry Pi Pico W. Based around the RP2040 microcontroller the Pico W is a low cost microcontroller device bringing Raspberry Pi quality, cost, and easy of use to the microcontroller space. The areas marked KEEPOUT in pcb silkscreen should not have traces running through them to avoid shorts on a soldered in module!
