# Fritzing sketch breadboard_layouts (saved by Fritzing 1.0.1rc)
breadboards: 6

parts:
  R18 = Resistor [tolerance=±5% resistance=1k package="0603 [SMD]"]
  R19 = Resistor [tolerance=±5% resistance=100k package="0603 [SMD]"]
  R20 = Resistor [tolerance=±5% resistance=1k package="0603 [SMD]"]
  LED6 = smd LED [color="Red (633nm)" package="1206 [SMD]"]
  Q7 = PNP-Transistor [package="TO92 [THT]"]
  D4 = Diode [package=diode-1n4001]
  Multimeter7 = Multimeter
  R24 = Resistor [tolerance=±5% resistance=100k package="0603 [SMD]"]
  R25 = Resistor [tolerance=±5% resistance=1k package="0603 [SMD]"]
  R26 = Resistor [tolerance=±5% resistance=1k package="0603 [SMD]"]
  Q9 = PNP-Transistor [package="TO92 [THT]"]
  D6 = Diode [package=diode-1n4001]
  U5 = Sharp PC817 [package=THT]
  Relay_SPST4 = Relay SPST
  Multimeter10 = Multimeter
  Multimeter11 = Multimeter
  Mod2 = Raspberry Pi Pico W
  LED4 = smd LED [color="Red (633nm)" package="1206 [SMD]"]
  R11 = Resistor [tolerance=±5% resistance=1k package="0603 [SMD]"]
  R12 = Resistor [tolerance=±5% resistance=1k package="0603 [SMD]"]
  Multimeter5 = Multimeter
  U3 = Sharp PC817 [package=THT]
  Mod4 = Raspberry Pi Pico W
  R27 = Resistor [tolerance=±5% resistance=1k package="0603 [SMD]"]
  R28 = Resistor [tolerance=±5% resistance=100k package="0603 [SMD]"]
  R29 = Resistor [tolerance=±5% resistance=100k package="0603 [SMD]"]
  R30 = Resistor [tolerance=±5% resistance=1k package="0603 [SMD]"]
  R31 = Resistor [tolerance=±5% resistance=1k package="0603 [SMD]"]
  R32 = Resistor [tolerance=±5% resistance=1k package="0603 [SMD]"]
  LED7 = smd LED [color="Red (633nm)" package="1206 [SMD]"]
  LED8 = smd LED [color="Red (633nm)" package="1206 [SMD]"]
  Q10 = PNP-Transistor [package="TO92 [THT]"]
  R33 = Resistor [tolerance=±5% resistance=1k package="0603 [SMD]"]
  R34 = Resistor [tolerance=±5% resistance=1k package="0603 [SMD]"]
  Q11 = PNP-Transistor [package="TO92 [THT]"]
  D7 = Diode [package=diode-1n4001]
  D8 = Diode [package=diode-1n4001]
  U6 = Sharp PC817 [package=THT]
  U7 = Sharp PC817 [package=THT]
  Relay_SPST5 = Relay SPST
  Multimeter12 = Multimeter
  Multimeter13 = Multimeter
  Multimeter14 = Multimeter
  Multimeter15 = Multimeter
  Mod6 = Raspberry Pi Pico W
  Mod1 = Raspberry Pi 5
  Mod3 = Raspberry Pi 5
  Mod5 = Raspberry Pi 5

nets:
  N1: R18.Pin_0, LED6.cathode, D4.A
  N2: R18.Pin_1, Q7.B
  N3: R19.Pin_0, R20.Pin_1, Q7.C
  N4: R19.Pin_1, Q7.E, Multimeter7.Com, Mod2.pin_38, Mod2.pin_42
  N5: R20.Pin_0, Mod2.pin_27
  N6: LED6.anode, D4.C, Multimeter7.Positive
  N7: R24.Pin_0, Q9.E, Multimeter11.Com
  N8: R24.Pin_1, R26.Pin_0, Q9.C
  N9: R25.Pin_0, U5.Pin_1
  N10: R25.Pin_1, Mod4.pin_36
  N11: R26.Pin_1, U5.Pin_3
  N12: Q9.B, Relay_SPST4.Coil#3
  N13: D6.C, U5.Pin_4, Relay_SPST4.Coil#4, Multimeter11.Positive
  N14: U5.Pin_2, Mod4.pin_27
  N15: Relay_SPST4.Com, Multimeter10.Com
  N16: LED4.cathode, R11.Pin_1
  N17: LED4.anode, Multimeter5.Positive
  N18: R11.Pin_0, U3.Pin_4
  N19: R12.Pin_0, U3.Pin_1
  N20: R12.Pin_1, Mod6.pin_36
  N21: Multimeter5.Com, U3.Pin_3
  N22: U3.Pin_2, Mod6.pin_27
  N23: R27.Pin_0, LED7.cathode, D7.A
  N24: R27.Pin_1, Q10.B
  N25: R28.Pin_0, R30.Pin_1, Q10.C
  N26: R28.Pin_1, Q10.E, Multimeter14.Com, Mod1.GND
  N27: R29.Pin_0, Q11.E, Multimeter12.Com
  N28: R29.Pin_1, R34.Pin_0, Q11.C
  N29: R30.Pin_0, Mod1.GPIO21
  N30: R31.Pin_0, U6.Pin_1
  N31: R31.Pin_1, Mod5.3V3
  N32: R32.Pin_0, U6.Pin_4
  N33: R32.Pin_1, LED8.cathode
  N34: LED7.anode, D7.C, Multimeter14.Positive
  N35: LED8.anode, Multimeter15.Positive
  N36: R33.Pin_0, U7.Pin_1
  N37: R33.Pin_1, Mod3.3V3
  N38: R34.Pin_1, U7.Pin_3
  N39: Q11.B, Relay_SPST5.Coil#3
  N40: D8.C, U7.Pin_4, Relay_SPST5.Coil#4, Multimeter12.Positive
  N41: U6.Pin_2, Mod5.GPIO21
  N42: U6.Pin_3, Multimeter15.Com
  N43: U7.Pin_2, Mod3.GPIO21
  N44: Relay_SPST5.Com, Multimeter13.Com

notes:
  S G D
  5
  Coil
  Relay Coil Power
  .
  L+
  L-
  Load
  Load Power
  External Power Source
  USB

custom parts:
  Multimeter: Blank Multimeter
  Raspberry Pi Pico W: Raspberry Pi Pico W. Based around the RP2040 microcontroller the Pico W is a low cost microcontroller device bringing Raspberry Pi quality, cost, and easy of use to the microcontroller space. The areas marked KEEPOUT in pcb silkscreen should not have traces running through them to avoid shorts on a soldered in module!
  Raspberry Pi 5: The RPi5, a faster version of the awesome Raspberry Pi4B ARM Board with 40 pin gpio.
