# Fritzing sketch breadboard_layouts (saved by Fritzing 1.0.1rc)
breadboards: 8

parts:
  DHT1 = DHT11 Humitidy and Temperature Sensor
  R1 = Resistor [tolerance=±5% resistance=10k package="2010 [SMD]"]
  R5 = Resistor [tolerance=±5% resistance=10k package="2010 [SMD]"]
  R6 = Resistor [tolerance=±5% resistance=1k package="2010 [SMD]"]
  Part2 = Adafruit ADS1115 16Bit I2C ADC [part_number="Adafruit #1085"]
  LED2 = LED - 5mm [color="Red (633nm)" current=0.030A package="5 mm [THT]"]
  R7 = Photocell (LDR) [power=0.25W dark_resistance_@0.01lx=300kΩ light_resistance_@100lx=400Ω luminance=10lx package=THT]
  R10 = Resistor [tolerance=±5% resistance=1k package="2010 [SMD]"]
  R11 = Resistor [tolerance=±5% resistance=10k package="2010 [SMD]"]
  LED4 = LED - 5mm [color="Red (633nm)" current=0.030A package="5 mm [THT]"]
  R12 = Resistor [tolerance=±5% resistance=1k package="2010 [SMD]"]
  R13 = Resistor [tolerance=±5% resistance=10k package="2010 [SMD]"]
  LED5 = LED - 5mm [color="Red (633nm)" current=0.030A package="5 mm [THT]"]
  R14 = Photocell (LDR) [power=0.25W dark_resistance_@0.01lx=300kΩ light_resistance_@100lx=400Ω luminance=10lx package=THT]
  Part3 = Adafruit ADS1115 16Bit I2C ADC [part_number="Adafruit #1085"]
  R9 = Resistor [tolerance=±5% resistance=1k package="2010 [SMD]"]
  R8 = Resistor [tolerance=±5% resistance=10k package="2010 [SMD]"]
  LED3 = LED - 5mm [color="Red (633nm)" current=0.030A package="5 mm [THT]"]
  DHT2 = DHT11 Humitidy and Temperature Sensor
  R15 = Resistor [tolerance=±5% resistance=10k package="2010 [SMD]"]
  R16 = Resistor [tolerance=±5% resistance=1k package="2010 [SMD]"]
  R17 = Resistor [tolerance=±5% resistance=10k package="2010 [SMD]"]
  Part4 = Adafruit ADS1115 16Bit I2C ADC [part_number="Adafruit #1085"]
  LED6 = LED - 5mm [color="Red (633nm)" current=0.030A package="5 mm [THT]"]
  R18 = Photocell (LDR) [power=0.25W dark_resistance_@0.01lx=300kΩ light_resistance_@100lx=400Ω luminance=10lx package=THT]
  R19 = Resistor [tolerance=±5% resistance=1k package="2010 [SMD]"]
  R20 = Resistor [tolerance=±5% resistance=10k package="2010 [SMD]"]
  Part5 = Adafruit ADS1115 16Bit I2C ADC [part_number="Adafruit #1085"]
  LED7 = LED - 5mm [color="Red (633nm)" current=0.030A package="5 mm [THT]"]
  Mod1 = Raspberry Pi Pico W
  Mod2 = Raspberry Pi Pico W
  Mod3 = Raspberry Pi Pico W
  Mod4 = Raspberry Pi Pico W
  Mod5 = Raspberry Pi Pico W
  A1 = Raspberry Pi 5
  A2 = Raspberry Pi 5
  A3 = Raspberry Pi 5

nets:
  VDD: DHT1.VDD, R1.Pin_1, A1.3V3
  N1: DHT1.DATA, R1.Pin_0, A1.GPIO21
  GND: DHT1.GND, A1.GND
  N2: R5.Pin_0, R6.Pin_1, Part2.GND, Mod3.pin_28, Mod3.pin_42
  N3: R5.Pin_1, Part2.AIN0, R7.pin_1
  N4: R6.Pin_0, LED2.cathode
  N5: Part2.SDA, Mod3.pin_21
  N6: Part2.SCL, Mod3.pin_22
  N7: Part2.VDD, R7.pin_0, Mod3.pin_36
  N8: LED2.anode, Mod3.pin_27
  N9: R10.Pin_0, LED4.cathode
  N10: R10.Pin_1, R11.Pin_0, Mod5.pin_28, Mod5.pin_42
  N11: R11.Pin_1, Mod5.pin_31
  N12: LED4.anode, Mod5.pin_27
  N13: R12.Pin_0, LED5.cathode
  N14: R12.Pin_1, R13.Pin_0, Mod2.pin_28, Mod2.pin_42
  N15: R13.Pin_1, R14.pin_1, Mod2.pin_31
  N16: LED5.anode, Mod2.pin_27
  N17: R14.pin_0, Mod2.pin_36
  N18: Part3.AIN0, R8.Pin_1
  N19: Part3.SDA, A3.GPIO2
  N20: Part3.SCL, A3.GPIO3
  GND_2: Part3.GND, R9.Pin_1, R8.Pin_0, A3.GND
  VDD_2: Part3.VDD, A3.3V3
  N21: R9.Pin_0, LED3.cathode
  N22: DHT2.VDD, R15.Pin_1, Mod1.pin_36
  N23: DHT2.DATA, R15.Pin_0, Mod1.pin_27
  N24: DHT2.GND, Mod1.pin_28, Mod1.pin_42
  N25: R16.Pin_0, LED6.cathode
  GND_3: R16.Pin_1, R17.Pin_0, Part4.GND, A2.GND
  N26: R17.Pin_1, Part4.AIN0, R18.pin_1
  N27: Part4.SDA, A2.GPIO2
  N28: Part4.SCL, A2.GPIO3
  VDD_3: Part4.VDD, R18.pin_0, A2.3V3
  N29: LED6.anode, A2.GPIO21
  N30: R19.Pin_0, LED7.cathode
  N31: R19.Pin_1, R20.Pin_0, Part5.GND, Mod4.pin_28, Mod4.pin_42
  N32: R20.Pin_1, Part5.AIN0
  N33: Part5.SDA, Mod4.pin_21
  N34: Part5.SCL, Mod4.pin_22
  N35: Part5.VDD, Mod4.pin_36
  N36: LED7.anode, Mod4.pin_27

notes:
  DATA
  Vcc
  NC
  GND

custom parts:
  DHT11 Humitidy and Temperature Sensor: DHT11 Humidity and Temperature Sensor
  Adafruit ADS1115 16Bit I2C ADC: For microcontrollers without an analog-to-digital converter or when you want a higher-precision ADC, the ADS1115 provides 16-bit precision at 860 samples/second over I2C. The chip can be configured as 4 single-ended input channels, or two differential channels. As a nice bonus, it even includes a programmable gain amplifier, up to x16, to help boost up smaller single/differential signals to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
  Raspberry Pi Pico W: Raspberry Pi Pico W. Based around the RP2040 microcontroller the Pico W is a low cost microcontroller device bringing Raspberry Pi quality, cost, and easy of use to the microcontroller space. The areas marked KEEPOUT in pcb silkscreen should not have traces running through them to avoid shorts on a soldered in module!
  Raspberry Pi 5: The RPi5, a faster version of the awesome Raspberry Pi4B ARM Board with 40 pin gpio.
